# Fritzing sketch rc car project (saved by Fritzing 0.9.3b)
breadboards: 1

parts:
  Part1 = Arduino Uno (Rev3)
  IC1 = L293D [package=THT]
  VCC1 = Battery block 9V
  M2 = DC Motor
  M1 = DC Motor

nets:
  N1: Part1.D2, IC1.Enable_1
  N2: Part1.D3_PWM, IC1.In_1
  N3: Part1.D4, IC1.In_2
  N4: Part1.D5_PWM, IC1.Enable_2
  N5: Part1.D6_PWM, IC1.In_3
  N6: Part1.D7, IC1.In_4
  N7: Part1.5V, IC1.+V
  N8: Part1.GND, IC1.0V, VCC1.-
  N9: IC1.Out_1_(_Controlled_by_Enable_1_), M2.pin_1
  N10: IC1.Out_2_(_Controlled_by_Enable_1_), M2.pin_2
  N11: IC1.+Vmotor, VCC1.+
  N12: IC1.Out_3_(_Controlled_by_Enable_2_), M1.pin_2
  N13: IC1.Out_4_(_Controlled_by_Enable_2_), M1.pin_1

// code stored in the sketch: rc car project.ino
int pins[] = {2, 3, 4, 5, 6, 7};
int input = 0;

void setup()
{
  for (int i = 0; i < 6; i++)
  {
    pinMode(pins[i], OUTPUT);
  }
  Serial.begin(9600);
  digitalWrite(7, 1);
  digitalWrite(6, 0);
  analogWrite(5, 0);
  digitalWrite(4, 0);
  digitalWrite(3, 1);
  analogWrite(2, 0);
}

void loop()
{
  sinput();
}

void mf() //move fast
{
  analogWrite(5, 255);
  analogWrite(2, 255);
}

void ms() //move slow
{
  
}

void tr() //turn right
{
  analogWrite(5, 0);
  analogWrite(2, 255);
}

void tl() //turn left
{
  analogWrite(5, 255);
  analogWrite(2, 0);
}
        
void b() //brake
{
  analogWrite(5, 0);
  analogWrite(2, 0);
}

void c() //coast
{
  for (int i = 0; i <= 255; i++)
  {
  	analogWrite(5, i);
  	analogWrite(2, i);
    
    if (i == 255)
    {
      analogWrite(5, 255);
      analogWrite(2, 255);
    }
  }
}

void sinput()
{
  Serial.println("1 - FAST");
  Serial.println("2 - SLOW");
  Serial.println("3 - TURN RIGHT");
  Serial.println("4 - TURN LEFT");
  Serial.println("5 - BRAKE");
  Serial.println("6 - COAST");
  
  while(Serial.available() == 0){}
  input = Serial.parseInt();
  
  if (input == 1)
  {
    mf();
  }
  else if (input == 2)
  {
    ms();
  }
  else if (input == 3)
  {
    tr();
  }
  else if (input == 4)
  {
    tl();
  }
  else if (input == 5)
  {
    b();
  }
  else if (input == 6)
  {
    c();
  }
  else
  {
    Serial.print("Not and option!")
  }
}
